# Fritzing sketch SmartHome (saved by Fritzing 0.9.4)
breadboards: 1

parts:
  WeMos_D1_Mini1 = WeMos D1 Mini
  KY-1 = Keyes Relay [package=THT]
  DHT11_1 = DHT11 module

nets:
  5V: WeMos_D1_Mini1.5V, KY-1.signal, DHT11_1.VCC
  N1: WeMos_D1_Mini1.D1, KY-1.ground
  N2: WeMos_D1_Mini1.D2, DHT11_1.DATA
  N3: WeMos_D1_Mini1.G, KY-1.power, DHT11_1.GND

custom parts:
  Keyes Relay: The Keyes 5V relay module is suitable for SCM development, home appliance control. It uses a 5V~12V TIL control signal which can control DC / AC signal.
  DHT11 module: DHT11 black pcb module
